# Fritzing sketch sensorPIR (saved by Fritzing 0.9.5d)

parts:
  Part1 = ESP-WROOM-32 [ESP-32S] Module [part_number=ESP-WROOM-32]
  PIR1 = PIR sensor

nets:
  GND: Part1.GND, PIR1.GND
  3V3: Part1.3V3, PIR1.VDD
  N1: Part1.IO18, PIR1.SIG

custom parts:
  ESP-WROOM-32 [ESP-32S] Module: Espressif ESP-WROOM-32 WiFi/Bluetooth LE microcontroller module also known as the Ai-Thinker ESP-32S module with similar formfactor. The ESP32 is a microcontroller chip with WiFi and BLE capabilities. The chip is developed by Espressif and is the successor to the popular ESP8266 WiFi module.
